# Fritzing sketch fritzing (saved by Fritzing 0.9.5d)
breadboards: 1

parts:
  Součástka1 = SparkFun ESP8266 Thing
  U1 = mystery part, 4 pins [chip_label=LM75]

nets:
  N1: Součástka1.GND, U1.pin4
  N2: Součástka1.GPIO2, U1.pin2
  N3: Součástka1.GPIO14, U1.pin3
  N4: Součástka1.USBVCC, U1.pin1
